# Fritzing sketch circuit (saved by Fritzing 0.9.3b)
breadboards: 1

parts:
  U1 = NodeMCU V1.0
  M1 = Dagu DGServo 9g (Top view) [part_number=RS001B]
  R3 = Resistor [tolerance=±5% resistance=4.7k package="0603 [SMD]"]
  DS3 = DS18B20 1-Wire Temperature Sensor [part_number=DS18B20]

nets:
  N1: U1.D1, M1.pulse
  N2: U1.D4, R3.Pin_1, DS3.DQ
  3V3: U1.3V3, M1.vcc, R3.Pin_0, DS3.VDD
  GND: U1.GND, M1.gnd, DS3.GND

custom parts:
  NodeMCU V1.0: ESP8266 based NodeMCU
